// Logisim project smips.circ as structural Verilog: 5 circuits, main circuit Board
module Board (
);

  wire CLK, HALT, MEM_WE, RESET, TTY_WE;
  wire [3:0] MEM_BE;
  wire [6:0] TTY_DATA;
  wire [31:0] MEM_ADDR, MEM_RDATA, MEM_WDATA;

  Clock Reloj (.out(CLK));
  Button u_Reset (.out(RESET));
  CPU cpu_1 (
    .CLK(CLK), .RESET(RESET), .MEM_RDATA(MEM_RDATA), .MEM_ADDR(MEM_ADDR), .MEM_WDATA(MEM_WDATA),
    .MEM_BE(MEM_BE), .MEM_WE(MEM_WE), .TTY_DATA(TTY_DATA), .TTY_WE(TTY_WE), .HALT(HALT));
  TTY #(.cols(48), .rows(12)) tty_1 (.data(TTY_DATA), .clk(CLK), .we(TTY_WE), .clr(RESET));
  Memory memory_1 (.CLK(CLK), .ADDR(MEM_ADDR), .WDATA(MEM_WDATA), .BE(MEM_BE), .WE(MEM_WE), .RDATA(MEM_RDATA));
  LED u_Halt (.in(HALT));

  // Notes on the sheet:
  //   S-MIPS | Board
  //   No modificar: la CPU se implementa dentro del subcircuito CPU.
endmodule

module CPU (
  input  CLK,
  input  RESET,
  input  [31:0] MEM_RDATA,
  output [31:0] MEM_ADDR,
  output [31:0] MEM_WDATA,
  output [3:0] MEM_BE,
  output MEM_WE,
  output [6:0] TTY_DATA,
  output TTY_WE,
  output HALT
);


  // Notes on the sheet:
  //   CPU S-MIPS: implementar aqui
  //   No cambiar nombres, anchos ni sentido de los pines: la placa depende de ellos.
endmodule

module Memory (
  input  CLK,
  input  [31:0] ADDR,
  input  [31:0] WDATA,
  input  [3:0] BE,
  input  WE,
  output [31:0] RDATA
);

  RAM #(.addrWidth(12), .asyncread("true"), .byteenables("byteEnables"), .dataWidth(32), .\type ("nonvolatile")) Main_Memory (
    .addr(ADDR[13:2]), .we(WE), .oe(1'b1), .clk(CLK), .din(WDATA), .dout(RDATA), .be3(BE[3]), .be2(BE[2]),
    .be1(BE[1]), .be0(BE[0]));

  // Other names for the same wires on the sheet: A[11:0] = ADDR[13:2]

  // Notes on the sheet:
  //   Memoria unificada: 4096 palabras de 32 bits (16 KiB), little-endian
  //   Lectura combinacional; escritura en el flanco de subida de CLK con WE=1, solo en los bytes con BE=1.
  //   Se usan los bits 13..2 de ADDR; los demas se ignoran (el espacio se repite cada 16 KiB).
endmodule

module ALU (
  input  [31:0] A,
  input  [31:0] B,
  input  [2:0] ALU_Op,
  output Zero,
  output [31:0] Result
);

  wire comparator_1_lt;
  wire [31:0] RES_ADD, RES_AND, RES_OR, RES_SLL, RES_SLT, RES_SRL, RES_SUB;

  Adder #(.width(32)) adder_1 (.a(A), .b(B), .out(RES_ADD));  // open: cin, cout
  Subtractor #(.width(32)) subtractor_1 (.a(A), .b(B), .out(RES_SUB));  // open: bin, bout
  assign RES_AND = A & B;  // AND_Gate and_1, 32 bits wide
  assign RES_OR = A | B;  // OR_Gate or_1, 32 bits wide
  Comparator #(.width(32)) comparator_1 (.a(A), .b(B), .lt(comparator_1_lt));  // open: gt, eq
  Shifter #(.width(32)) shifter_1 (.in(A), .\dist (B[4:0]), .out(RES_SLL));
  Shifter #(.shift("lr"), .width(32)) shifter_2 (.in(A), .\dist (B[4:0]), .out(RES_SRL));
  assign RES_SLT = {{31{comparator_1_lt}}, comparator_1_lt};  // Bit_Extender bit_extender_1
  Comparator #(.width(32)) comparator_2 (.a(Result), .b({32{1'b0}}), .eq(Zero));  // open: gt, lt
  Multiplexer #(.select(3), .width(32)) multiplexer_1 (
    .in0(RES_ADD), .in1(RES_SUB), .in2(RES_AND), .in3(RES_OR), .in4(RES_SLT), .in5(RES_SLL), .in6(RES_SRL),
    .out(Result), .sel(ALU_Op));  // open: in7

  // Other names for the same wires on the sheet: SHAMT[4:0] = B[4:0]
endmodule

module Register_File (
  input  CLK,
  input  RESET,
  input  [31:0] Write_Data,
  input  RegWrite,
  input  [4:0] Write_Reg,
  input  [4:0] Read_Reg1,
  input  [4:0] Read_Reg2,
  output [31:0] Read_Data1,
  output [31:0] Read_Data2
);

  wire decoder_1_out0, EN_R1, EN_R2, EN_R3, EN_R4, EN_R5, EN_R6, EN_R7, EN_R8, EN_R9, EN_R10, EN_R11, EN_R12,
       EN_R13, EN_R14, EN_R15, EN_R16, EN_R17, EN_R18, EN_R19, EN_R20, EN_R21, EN_R22, EN_R23, EN_R24,
       EN_R25, EN_R26, EN_R27, EN_R28, EN_R29, EN_R30, EN_R31, or_1_out, or_2_out;
  wire [31:0] multiplexer_1_out, multiplexer_2_out, R1_OUT, R2_OUT, R3_OUT, R4_OUT, R5_OUT, R6_OUT, R7_OUT,
       R8_OUT, R9_OUT, R10_OUT, R11_OUT, R12_OUT, R13_OUT, R14_OUT, R15_OUT, R16_OUT, R17_OUT, R18_OUT,
       R19_OUT, R20_OUT, R21_OUT, R22_OUT, R23_OUT, R24_OUT, R25_OUT, R26_OUT, R27_OUT, R28_OUT, R29_OUT,
       R30_OUT, R31_OUT;

  Decoder #(.select(5)) decoder_1 (
    .out0(decoder_1_out0), .out1(EN_R1), .out2(EN_R2), .out3(EN_R3), .out4(EN_R4), .out5(EN_R5),
    .out6(EN_R6), .out7(EN_R7), .out8(EN_R8), .out9(EN_R9), .out10(EN_R10), .out11(EN_R11), .out12(EN_R12),
    .out13(EN_R13), .out14(EN_R14), .out15(EN_R15), .out16(EN_R16), .out17(EN_R17), .out18(EN_R18),
    .out19(EN_R19), .out20(EN_R20), .out21(EN_R21), .out22(EN_R22), .out23(EN_R23), .out24(EN_R24),
    .out25(EN_R25), .out26(EN_R26), .out27(EN_R27), .out28(EN_R28), .out29(EN_R29), .out30(EN_R30),
    .out31(EN_R31), .sel(Write_Reg), .en(RegWrite));
  Multiplexer #(.width(32)) multiplexer_1 (.in0(Write_Data), .in1(32'h1800), .out(multiplexer_1_out), .sel(RESET));
  Register #(.width(32)) register_1 (.D(multiplexer_1_out), .en(or_1_out), .clk(CLK), .Q(R28_OUT), .clr(1'b0));
  or or_1 (or_1_out, RESET, EN_R28);
  Register #(.width(32)) register_2 (.D(Write_Data), .en(EN_R4), .clk(CLK), .Q(R4_OUT), .clr(RESET));
  Register #(.width(32)) register_3 (.D(Write_Data), .en(EN_R8), .clk(CLK), .Q(R8_OUT), .clr(RESET));
  Register #(.width(32)) register_4 (.D(Write_Data), .en(EN_R12), .clk(CLK), .Q(R12_OUT), .clr(RESET));
  Register #(.width(32)) register_5 (.D(Write_Data), .en(EN_R16), .clk(CLK), .Q(R16_OUT), .clr(RESET));
  Register #(.width(32)) register_6 (.D(Write_Data), .en(EN_R20), .clk(CLK), .Q(R20_OUT), .clr(RESET));
  Register #(.width(32)) register_7 (.D(Write_Data), .en(EN_R24), .clk(CLK), .Q(R24_OUT), .clr(RESET));
  Multiplexer #(.width(32)) multiplexer_2 (.in0(Write_Data), .in1(32'h3ffc), .out(multiplexer_2_out), .sel(RESET));
  or or_2 (or_2_out, RESET, EN_R29);
  Register #(.width(32)) register_8 (.D(Write_Data), .en(EN_R1), .clk(CLK), .Q(R1_OUT), .clr(RESET));
  Register #(.width(32)) register_9 (.D(Write_Data), .en(EN_R5), .clk(CLK), .Q(R5_OUT), .clr(RESET));
  Register #(.width(32)) register_10 (.D(Write_Data), .en(EN_R9), .clk(CLK), .Q(R9_OUT), .clr(RESET));
  Register #(.width(32)) register_11 (.D(Write_Data), .en(EN_R13), .clk(CLK), .Q(R13_OUT), .clr(RESET));
  Register #(.width(32)) register_12 (.D(Write_Data), .en(EN_R17), .clk(CLK), .Q(R17_OUT), .clr(RESET));
  Register #(.width(32)) register_13 (.D(Write_Data), .en(EN_R21), .clk(CLK), .Q(R21_OUT), .clr(RESET));
  Register #(.width(32)) register_14 (.D(Write_Data), .en(EN_R25), .clk(CLK), .Q(R25_OUT), .clr(RESET));
  Register #(.width(32)) register_15 (.D(multiplexer_2_out), .en(or_2_out), .clk(CLK), .Q(R29_OUT), .clr(1'b0));
  Register #(.width(32)) register_16 (.D(Write_Data), .en(EN_R2), .clk(CLK), .Q(R2_OUT), .clr(RESET));
  Register #(.width(32)) register_17 (.D(Write_Data), .en(EN_R6), .clk(CLK), .Q(R6_OUT), .clr(RESET));
  Register #(.width(32)) register_18 (.D(Write_Data), .en(EN_R10), .clk(CLK), .Q(R10_OUT), .clr(RESET));
  Register #(.width(32)) register_19 (.D(Write_Data), .en(EN_R14), .clk(CLK), .Q(R14_OUT), .clr(RESET));
  Register #(.width(32)) register_20 (.D(Write_Data), .en(EN_R18), .clk(CLK), .Q(R18_OUT), .clr(RESET));
  Register #(.width(32)) register_21 (.D(Write_Data), .en(EN_R22), .clk(CLK), .Q(R22_OUT), .clr(RESET));
  Register #(.width(32)) register_22 (.D(Write_Data), .en(EN_R26), .clk(CLK), .Q(R26_OUT), .clr(RESET));
  Register #(.width(32)) register_23 (.D(Write_Data), .en(EN_R30), .clk(CLK), .Q(R30_OUT), .clr(RESET));
  Register #(.width(32)) register_24 (.D(Write_Data), .en(EN_R3), .clk(CLK), .Q(R3_OUT), .clr(RESET));
  Register #(.width(32)) register_25 (.D(Write_Data), .en(EN_R7), .clk(CLK), .Q(R7_OUT), .clr(RESET));
  Register #(.width(32)) register_26 (.D(Write_Data), .en(EN_R11), .clk(CLK), .Q(R11_OUT), .clr(RESET));
  Register #(.width(32)) register_27 (.D(Write_Data), .en(EN_R15), .clk(CLK), .Q(R15_OUT), .clr(RESET));
  Register #(.width(32)) register_28 (.D(Write_Data), .en(EN_R19), .clk(CLK), .Q(R19_OUT), .clr(RESET));
  Register #(.width(32)) register_29 (.D(Write_Data), .en(EN_R23), .clk(CLK), .Q(R23_OUT), .clr(RESET));
  Register #(.width(32)) register_30 (.D(Write_Data), .en(EN_R27), .clk(CLK), .Q(R27_OUT), .clr(RESET));
  Register #(.width(32)) register_31 (.D(Write_Data), .en(EN_R31), .clk(CLK), .Q(R31_OUT), .clr(RESET));
  Multiplexer #(.select(5), .width(32)) multiplexer_3 (
    .in0({32{1'b0}}), .in1(R1_OUT), .in2(R2_OUT), .in3(R3_OUT), .in4(R4_OUT), .in5(R5_OUT), .in6(R6_OUT),
    .in7(R7_OUT), .in8(R8_OUT), .in9(R9_OUT), .in10(R10_OUT), .in11(R11_OUT), .in12(R12_OUT), .in13(R13_OUT),
    .in14(R14_OUT), .in15(R15_OUT), .in16(R16_OUT), .in17(R17_OUT), .in18(R18_OUT), .in19(R19_OUT),
    .in20(R20_OUT), .in21(R21_OUT), .in22(R22_OUT), .in23(R23_OUT), .in24(R24_OUT), .in25(R25_OUT),
    .in26(R26_OUT), .in27(R27_OUT), .in28(R28_OUT), .in29(R29_OUT), .in30(R30_OUT), .in31(R31_OUT),
    .out(Read_Data1), .sel(Read_Reg1));
  Multiplexer #(.select(5), .width(32)) multiplexer_4 (
    .in0({32{1'b0}}), .in1(R1_OUT), .in2(R2_OUT), .in3(R3_OUT), .in4(R4_OUT), .in5(R5_OUT), .in6(R6_OUT),
    .in7(R7_OUT), .in8(R8_OUT), .in9(R9_OUT), .in10(R10_OUT), .in11(R11_OUT), .in12(R12_OUT), .in13(R13_OUT),
    .in14(R14_OUT), .in15(R15_OUT), .in16(R16_OUT), .in17(R17_OUT), .in18(R18_OUT), .in19(R19_OUT),
    .in20(R20_OUT), .in21(R21_OUT), .in22(R22_OUT), .in23(R23_OUT), .in24(R24_OUT), .in25(R25_OUT),
    .in26(R26_OUT), .in27(R27_OUT), .in28(R28_OUT), .in29(R29_OUT), .in30(R30_OUT), .in31(R31_OUT),
    .out(Read_Data2), .sel(Read_Reg2));
endmodule
